// Logisim project ym2610.circ as structural Verilog: 7 circuits, main circuit main
module main (
);

  wire controlled_buffer_1_out, undriven;
  wire [8:0] write_data_1_valout;

  write_data write_data_1 (.valout(write_data_1_valout));  // open: data_in, bank, write, oe, nvalout
  assign controlled_buffer_1_out = undriven ? write_data_1_valout[0] : 1'bz;  // Controlled_Buffer controlled_buffer_1
  assign controlled_buffer_1_out = undriven ? write_data_1_valout[1] : 1'bz;  // Controlled_Buffer controlled_buffer_2
  assign controlled_buffer_1_out = undriven ? write_data_1_valout[2] : 1'bz;  // Controlled_Buffer controlled_buffer_3
  assign controlled_buffer_1_out = undriven ? write_data_1_valout[3] : 1'bz;  // Controlled_Buffer controlled_buffer_4
  assign controlled_buffer_1_out = undriven ? write_data_1_valout[4] : 1'bz;  // Controlled_Buffer controlled_buffer_5
  assign controlled_buffer_1_out = undriven ? write_data_1_valout[5] : 1'bz;  // Controlled_Buffer controlled_buffer_6
  assign controlled_buffer_1_out = undriven ? write_data_1_valout[6] : 1'bz;  // Controlled_Buffer controlled_buffer_7
  assign controlled_buffer_1_out = undriven ? write_data_1_valout[7] : 1'bz;  // Controlled_Buffer controlled_buffer_8
  // also tied to GND on the sheet: controlled_buffer_1_out
endmodule

module sr_bit (
  input  val,
  input  clk1,
  input  clk2,
  output valout,
  output nvalout
);

  wire d_ff_1_q;

  D_Flip_Flop #(.trigger("high")) d_ff_1 (.D(val), .clk(clk1), .Q(d_ff_1_q));  // open: Qn, preset, reset
  D_Flip_Flop #(.trigger("high")) d_ff_2 (.D(d_ff_1_q), .clk(clk2), .Q(valout), .Qn(nvalout));  // open: preset, reset
endmodule

module reg_bit_1 (
  input  oe,
  input  val,
  input  write,
  output nvalout,
  output valout
);

  wire d_ff_1_q, nor_1_out, nor_2_out;

  D_Flip_Flop #(.trigger("high")) d_ff_1 (.D(val), .clk(write), .Q(d_ff_1_q));  // open: Qn, preset, reset
  nor nor_1 (nor_1_out, oe, d_ff_1_q);
  nor nor_2 (nor_2_out, oe, nor_1_out);
  assign nvalout = nor_1_out ? 1'b1 : 1'bz;  // Controlled_Buffer controlled_buffer_1
  assign nvalout = nor_2_out ? 1'b0 : 1'bz;  // Controlled_Buffer controlled_buffer_2
  assign valout = nor_2_out ? 1'b1 : 1'bz;  // Controlled_Buffer controlled_buffer_3
  assign valout = nor_1_out ? 1'b0 : 1'bz;  // Controlled_Buffer controlled_buffer_4

  // Notes on the sheet:
  //   dynamic latch!!!
endmodule

module read_bus_1 (
  input  val,
  input  enable,
  output valout
);

  wire nor_1_out, nor_2_out;

  nor nor_1 (nor_1_out, val, enable);
  nor nor_2 (nor_2_out, nor_1_out, enable);
  assign valout = nor_2_out ? 1'b1 : 1'bz;  // Controlled_Buffer controlled_buffer_1
  assign valout = nor_1_out ? 1'b0 : 1'bz;  // Controlled_Buffer controlled_buffer_2
endmodule

module write_data (
  input  [7:0] data_in,
  input  bank,
  input  write,
  input  oe,
  output [8:0] valout,
  output [8:0] nvalout
);

  reg_bit_1 reg_bit_1_1 (.oe(oe), .val(data_in[0]), .write(write), .nvalout(nvalout[0]), .valout(valout[0]));
  reg_bit_1 reg_bit_1_2 (.oe(oe), .val(data_in[1]), .write(write), .nvalout(nvalout[1]), .valout(valout[1]));
  reg_bit_1 reg_bit_1_3 (.oe(oe), .val(data_in[2]), .write(write), .nvalout(nvalout[2]), .valout(valout[2]));
  reg_bit_1 reg_bit_1_4 (.oe(oe), .val(data_in[3]), .write(write), .nvalout(nvalout[3]), .valout(valout[3]));
  reg_bit_1 reg_bit_1_5 (.oe(oe), .val(data_in[4]), .write(write), .nvalout(nvalout[4]), .valout(valout[4]));
  reg_bit_1 reg_bit_1_6 (.oe(oe), .val(data_in[5]), .write(write), .nvalout(nvalout[5]), .valout(valout[5]));
  reg_bit_1 reg_bit_1_7 (.oe(oe), .val(data_in[6]), .write(write), .nvalout(nvalout[6]), .valout(valout[6]));
  reg_bit_1 reg_bit_1_8 (.oe(oe), .val(data_in[7]), .write(write), .nvalout(nvalout[7]), .valout(valout[7]));
  reg_bit_1 reg_bit_1_9 (.oe(oe), .val(bank), .write(write), .nvalout(nvalout[8]), .valout(valout[8]));
endmodule

module clk_gen (
  input  MCLK,
  output clk1,
  output clk2
);

  wire not_1_out, not_2_out, not_3_out, not_4_out, not_5_out, not_6_out, not_7_out;

  not not_1 (not_1_out, MCLK);
  not not_2 (not_2_out, not_1_out);
  not not_3 (not_3_out, not_2_out);
  nor nor_1 (clk1, not_2_out, not_7_out);
  nor nor_2 (clk2, not_3_out, not_6_out);
  not not_4 (not_4_out, clk1);
  not not_5 (not_5_out, clk2);
  not not_6 (not_6_out, not_4_out);
  not not_7 (not_7_out, not_5_out);
endmodule

module clk_div (
  input  clk1,
  input  clk2,
  input  IC,
  output fm_clk1,
  output fm_clk2,
  output res_latch1,
  output res_latch2,
  output out_8,
  output out_9,
  output out_10,
  output out_11,
  output out_12,
  output out_13,
  output out_14
);

  wire nor_1_out, nor_2_out, nor_3_out, nor_4_out, nor_5_out, nor_6_out, nor_7_out, nor_8_out, nor_9_out,
       nor_10_out, nor_11_out, not_1_out, not_2_out, not_3_out, not_6_out, not_9_out, not_12_out, not_13_out,
       not_14_out, not_15_out, not_16_out, not_17_out, not_18_out, not_19_out, not_20_out, sr_bit_1_valout,
       sr_bit_2_valout, sr_bit_3_valout, sr_bit_4_valout, sr_bit_5_valout, sr_bit_6_valout, sr_bit_7_valout,
       sr_bit_8_valout, sr_bit_9_valout, sr_bit_10_valout, sr_bit_11_valout, sr_bit_12_valout,
       sr_bit_13_valout, sr_bit_14_valout, sr_bit_15_valout, sr_bit_16_valout, sr_bit_17_valout,
       sr_bit_18_valout, sr_bit_19_valout, sr_bit_20_valout, sr_bit_21_valout, sr_bit_22_valout,
       sr_bit_23_valout, sr_bit_24_valout, sr_bit_25_valout, sr_bit_26_valout, sr_bit_27_valout,
       sr_bit_28_valout, sr_bit_29_valout, sr_bit_30_valout, sr_bit_31_valout, sr_bit_32_valout,
       sr_bit_33_valout, sr_bit_34_valout, sr_bit_35_valout, sr_bit_36_valout, sr_bit_37_valout,
       sr_bit_38_valout, sr_bit_39_valout, sr_bit_40_valout, sr_bit_41_valout, sr_bit_42_valout;

  sr_bit sr_bit_1 (.clk1(clk1), .clk2(clk2), .val(IC), .valout(sr_bit_1_valout));  // open: nvalout
  nor nor_1 (nor_1_out, not_3_out, not_20_out);
  sr_bit sr_bit_2 (.clk1(clk1), .clk2(clk2), .val(sr_bit_1_valout), .valout(sr_bit_2_valout));  // open: nvalout
  sr_bit sr_bit_3 (.clk1(clk1), .clk2(clk2), .val(nor_1_out), .valout(sr_bit_3_valout));  // open: nvalout
  sr_bit sr_bit_4 (.clk1(clk1), .clk2(clk2), .val(sr_bit_2_valout), .valout(sr_bit_4_valout));  // open: nvalout
  not not_1 (not_1_out, sr_bit_1_valout);
  sr_bit sr_bit_5 (.clk1(clk1), .clk2(clk2), .val(sr_bit_3_valout), .valout(sr_bit_5_valout));  // open: nvalout
  sr_bit sr_bit_6 (.clk1(clk1), .clk2(clk2), .val(sr_bit_4_valout), .valout(sr_bit_6_valout));  // open: nvalout
  sr_bit sr_bit_7 (.clk1(clk1), .clk2(clk2), .val(sr_bit_6_valout), .valout(sr_bit_7_valout));  // open: nvalout
  nor nor_2 (nor_2_out, sr_bit_42_valout, not_1_out);
  not not_2 (not_2_out, nor_2_out);
  sr_bit sr_bit_8 (.clk1(clk1), .clk2(clk2), .val(sr_bit_5_valout), .valout(sr_bit_8_valout));  // open: nvalout
  sr_bit sr_bit_9 (.clk1(clk1), .clk2(clk2), .val(sr_bit_8_valout), .valout(sr_bit_9_valout));  // open: nvalout
  sr_bit sr_bit_10 (.clk1(clk1), .clk2(clk2), .val(sr_bit_7_valout), .valout(sr_bit_10_valout));  // open: nvalout
  sr_bit sr_bit_11 (.clk1(clk1), .clk2(clk2), .val(not_2_out), .valout(sr_bit_11_valout));  // open: nvalout
  sr_bit sr_bit_12 (.clk1(clk1), .clk2(clk2), .val(sr_bit_9_valout), .valout(sr_bit_12_valout));  // open: nvalout
  sr_bit sr_bit_13 (.clk1(clk1), .clk2(clk2), .val(sr_bit_10_valout), .valout(sr_bit_13_valout));  // open: nvalout
  sr_bit sr_bit_14 (.clk1(clk1), .clk2(clk2), .val(sr_bit_11_valout), .valout(sr_bit_14_valout));  // open: nvalout
  sr_bit sr_bit_15 (.clk1(clk1), .clk2(clk2), .val(sr_bit_12_valout), .valout(sr_bit_15_valout));  // open: nvalout
  sr_bit sr_bit_16 (.clk1(clk1), .clk2(clk2), .val(sr_bit_13_valout), .valout(sr_bit_16_valout));  // open: nvalout
  not not_3 (not_3_out, not_2_out);
  sr_bit sr_bit_17 (.clk1(clk1), .clk2(clk2), .val(sr_bit_14_valout), .valout(sr_bit_17_valout));  // open: nvalout
  sr_bit sr_bit_18 (.clk1(clk1), .clk2(clk2), .val(sr_bit_16_valout), .valout(sr_bit_18_valout));  // open: nvalout
  not not_4 (res_latch2, sr_bit_17_valout);
  sr_bit sr_bit_19 (.clk1(clk1), .clk2(clk2), .val(sr_bit_15_valout), .valout(sr_bit_19_valout));  // open: nvalout
  sr_bit sr_bit_20 (.clk1(clk1), .clk2(clk2), .val(sr_bit_18_valout), .valout(sr_bit_20_valout));  // open: nvalout
  sr_bit sr_bit_21 (.clk1(clk1), .clk2(clk2), .val(sr_bit_17_valout), .valout(sr_bit_21_valout));  // open: nvalout
  sr_bit sr_bit_22 (.clk1(clk1), .clk2(clk2), .val(sr_bit_19_valout), .valout(sr_bit_22_valout));  // open: nvalout
  sr_bit sr_bit_23 (.clk1(clk1), .clk2(clk2), .val(sr_bit_20_valout), .valout(sr_bit_23_valout));  // open: nvalout
  not not_5 (res_latch1, sr_bit_21_valout);
  sr_bit sr_bit_24 (.clk1(clk1), .clk2(clk2), .val(sr_bit_22_valout), .valout(sr_bit_24_valout));  // open: nvalout
  sr_bit sr_bit_25 (.clk1(clk1), .clk2(clk2), .val(sr_bit_23_valout), .valout(sr_bit_25_valout));  // open: nvalout
  sr_bit sr_bit_26 (.clk1(clk1), .clk2(clk2), .val(sr_bit_24_valout), .valout(sr_bit_26_valout));  // open: nvalout
  sr_bit sr_bit_27 (.clk1(clk1), .clk2(clk2), .val(sr_bit_25_valout), .valout(sr_bit_27_valout));  // open: nvalout
  sr_bit sr_bit_28 (.clk1(clk1), .clk2(clk2), .val(sr_bit_26_valout), .valout(sr_bit_28_valout));  // open: nvalout
  sr_bit sr_bit_29 (.clk1(clk1), .clk2(clk2), .val(sr_bit_27_valout), .valout(sr_bit_29_valout));  // open: nvalout
  sr_bit sr_bit_30 (.clk1(clk1), .clk2(clk2), .val(sr_bit_28_valout), .valout(sr_bit_30_valout));  // open: nvalout
  sr_bit sr_bit_31 (.clk1(clk1), .clk2(clk2), .val(sr_bit_29_valout), .valout(sr_bit_31_valout));  // open: nvalout
  sr_bit sr_bit_32 (.clk1(clk1), .clk2(clk2), .val(sr_bit_31_valout), .valout(sr_bit_32_valout));  // open: nvalout
  nor nor_3 (nor_3_out, sr_bit_3_valout, sr_bit_8_valout, sr_bit_12_valout, sr_bit_19_valout, sr_bit_24_valout, sr_bit_28_valout);
  not not_6 (not_6_out, nor_4_out);
  nor nor_4 (nor_4_out, sr_bit_8_valout, sr_bit_9_valout, sr_bit_12_valout, sr_bit_15_valout, sr_bit_19_valout, sr_bit_22_valout, sr_bit_24_valout, sr_bit_26_valout, sr_bit_28_valout, sr_bit_30_valout);
  nor nor_5 (nor_5_out, sr_bit_8_valout, sr_bit_9_valout, sr_bit_24_valout, sr_bit_26_valout);
  nor nor_6 (nor_6_out, sr_bit_3_valout, sr_bit_15_valout, sr_bit_19_valout, sr_bit_30_valout);
  nor nor_7 (nor_7_out, sr_bit_24_valout, sr_bit_26_valout, sr_bit_28_valout, sr_bit_30_valout);
  nor nor_8 (nor_8_out, sr_bit_3_valout, sr_bit_5_valout, sr_bit_8_valout, sr_bit_9_valout, sr_bit_12_valout, sr_bit_15_valout, sr_bit_19_valout, sr_bit_22_valout, sr_bit_24_valout, sr_bit_26_valout, sr_bit_28_valout);
  nor nor_9 (nor_9_out, sr_bit_3_valout, sr_bit_9_valout, sr_bit_19_valout, sr_bit_26_valout);
  nor nor_10 (nor_10_out, sr_bit_8_valout, sr_bit_9_valout, sr_bit_12_valout, sr_bit_15_valout);
  nor nor_11 (nor_11_out, sr_bit_8_valout, sr_bit_15_valout, sr_bit_24_valout, sr_bit_30_valout);
  sr_bit sr_bit_33 (.clk1(clk1), .clk2(clk2), .val(sr_bit_32_valout), .valout(sr_bit_33_valout));  // open: nvalout
  sr_bit sr_bit_34 (.clk1(clk1), .clk2(clk2), .val(nor_3_out), .valout(sr_bit_34_valout));  // open: nvalout
  D_Flip_Flop #(.trigger("high")) d_ff_1 (.D(not_6_out), .clk(clk1), .Qn(out_14));  // open: Q, preset, reset
  sr_bit sr_bit_35 (.clk1(clk1), .clk2(clk2), .val(nor_5_out), .valout(sr_bit_35_valout));  // open: nvalout
  sr_bit sr_bit_36 (.clk1(clk1), .clk2(clk2), .val(nor_6_out), .valout(sr_bit_36_valout));  // open: nvalout
  sr_bit sr_bit_37 (.clk1(clk1), .clk2(clk2), .val(nor_7_out), .valout(sr_bit_37_valout));  // open: nvalout
  sr_bit sr_bit_38 (.clk1(clk1), .clk2(clk2), .val(nor_9_out), .valout(sr_bit_38_valout));  // open: nvalout
  sr_bit sr_bit_39 (.clk1(clk1), .clk2(clk2), .val(nor_10_out), .valout(sr_bit_39_valout));  // open: nvalout
  sr_bit sr_bit_40 (.clk1(clk1), .clk2(clk2), .val(nor_11_out), .valout(sr_bit_40_valout));  // open: nvalout
  sr_bit sr_bit_41 (.clk1(clk1), .clk2(clk2), .val(sr_bit_33_valout), .valout(sr_bit_41_valout));  // open: nvalout
  not not_7 (out_12, sr_bit_37_valout);
  not not_8 (out_13, sr_bit_39_valout);
  sr_bit sr_bit_42 (.clk1(clk1), .clk2(clk2), .val(sr_bit_41_valout), .valout(sr_bit_42_valout));  // open: nvalout
  not not_9 (not_9_out, sr_bit_34_valout);
  nor nor_12 (out_8, sr_bit_34_valout, not_15_out);
  nor nor_13 (out_9, not_9_out, not_13_out);
  nor nor_14 (out_10, sr_bit_38_valout, not_19_out);
  nor nor_15 (out_11, sr_bit_40_valout, not_17_out);
  not not_10 (fm_clk2, sr_bit_35_valout);
  not not_11 (fm_clk1, sr_bit_36_valout);
  not not_12 (not_12_out, out_8);
  not not_13 (not_13_out, not_12_out);
  not not_14 (not_14_out, out_9);
  not not_15 (not_15_out, not_14_out);
  not not_16 (not_16_out, out_10);
  not not_17 (not_17_out, not_16_out);
  not not_18 (not_18_out, out_11);
  not not_19 (not_19_out, not_18_out);
  not not_20 (not_20_out, nor_8_out);
endmodule
